# Fritzing sketch slarm (saved by Fritzing 0.9.3b)
circuit board: 11.39cm x 6.52402cm

parts:
  元件1 = Arduino Nano (Rev3.0) (ICSP)
  Pololu_A1 = Pololu A4988 [package=SO16]
  ZS-042_RTC1 = ZS-042 RTC Module
  元件2 = Bluetooth HC-05 Macho
  M1 = Stepper Motor - Bipolar
  C1 = Capacitor Polarized [package=cpol-radial-10uf-25v]
  Power_plug1 = Power plug
  SP1 = SPEAKER [package=pcb_mount_speaker]
  R1 = Resistor [tolerance=±5% resistance=1k package=THT]
  DFRobot_DFPlayer_Mini1 = DFRobot DFPlayer Mini [part_number=DFR0299]
  R2 = Resistor [tolerance=±5% resistance=1k package=THT]
  元件3 = Adafruit I2C+SPI LCD Backpack [part_number="Adafruit #292"]
  U1 = LCD-16X2 [package=lcd-16x2_noholes]
  R3 = Resistor [tolerance=±5% resistance=10k package=THT]
  S1 = Square Pushbutton

nets:
  N1: 元件1.D1/TX, R1.Pin_0
  N2: 元件1.D0/RX, R2.Pin_0
  N3: 元件1.D2, R3.Pin_1, S1.leg0
  N4: 元件1.D3, 元件2.TXD
  N5: 元件1.D4, 元件2.RXD
  N6: 元件1.D8, Pololu_A1.DIR
  N7: 元件1.D9, Pololu_A1.STEP
  GND: 元件1.GND, Pololu_A1.GND#8, ZS-042_RTC1.GND, 元件2.GND, DFRobot_DFPlayer_Mini1.GND-1, DFRobot_DFPlayer_Mini1.GND-2, 元件3.GND, U1.DB5, U1.K
  VCC: 元件1.5V, Pololu_A1.VDD, ZS-042_RTC1.VCC, 元件2.VCC, DFRobot_DFPlayer_Mini1.VCC, 元件3.VCC, U1.VDD, U1.A, S1.leg1
  N8: 元件1.A5, ZS-042_RTC1.SCL, 元件3.CLOCK
  N9: 元件1.A4, ZS-042_RTC1.SDA, 元件3.DATA
  N10: 元件1.3V3, 元件2.Key
  N11: Pololu_A1.RESET, Pololu_A1.SLEEP
  N12: Pololu_A1.1B, M1.D
  N13: Pololu_A1.1A, M1.B
  N14: Pololu_A1.2A, M1.C
  N15: Pololu_A1.2B, M1.A
  N16: Pololu_A1.GND#14, C1.-, Power_plug1.GND
  N17: Pololu_A1.VMOT, C1.+, Power_plug1.VCC
  N18: SP1.+, DFRobot_DFPlayer_Mini1.SPK_2
  N19: SP1.-, DFRobot_DFPlayer_Mini1.SPK_1
  N20: R1.Pin_1, DFRobot_DFPlayer_Mini1.RX
  N21: DFRobot_DFPlayer_Mini1.TX, R2.Pin_1
  N22: 元件3.CONTRAST, U1.DB7
  N23: 元件3.RS, U1.DB6
  N24: 元件3.E, U1.DB4
  N25: 元件3.DB0, U1.DB3
  N26: 元件3.DB1, U1.DB2
  N27: 元件3.DB2, U1.DB1
  N28: 元件3.DB3, U1.DB0
  N29: 元件3.DB4, U1.E
  N30: 元件3.DB5, U1.R_W
  N31: 元件3.DB6, U1.RS
  N32: 元件3.DB7, U1.VO
  N33: 元件3.LEDK, U1.VSS

notes:
  Button
  DFPlayer mini
  DS3231
  HC-05
  A4988

custom parts:
  Adafruit I2C+SPI LCD Backpack: LCD backpacks reduce the number of pins needed to connect to an LCD. LCDs are a fun and easy way to have your microcontroller project talk back to you. Character LCDs are common, and easy to get, available in tons of colors and sizes. We've written tutorials on using character LCDs with an Arduino (or similar microcontroller) but find that the number of pins necessary to control the LCD can be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
